# Fritzing sketch hold (saved by Fritzing 0.9.0b)
breadboards: 1

parts:
  Part1 = Arduino Uno (Rev3)
  LCD1 = LCD screen
  S1 = Pushbutton [package="[THT]"]
  VCC1 = Battery
  IC2 = IC, DIP package, 18 pins [chip_label=MT8870DE]
  XTAL1 = Crystal [frequency="4 MHz" part_number=3.579545MHz package=THT]
  MIC1 = Microphone
  C1 = Ceramic Capacitor [capacitance=100nF package="100 mil [THT, multilayer]"]
  R1 = Resistor [tolerance=±5% resistance=220 package=THT]
  R2 = Resistor [tolerance=±5% resistance=220 package=THT]
  R3 = Resistor [tolerance=±5% resistance=220 package=THT]
  C2 = Ceramic Capacitor [capacitance=100nF package="100 mil [THT, multilayer]"]
  R4 = Resistor [tolerance=±5% resistance=5.1k package=THT]

nets:
  N1: Part1.A0, IC2.pin11
  N2: Part1.A1, IC2.pin12
  N3: Part1.A2, IC2.pin13
  N4: Part1.A3, IC2.pin14
  N5: Part1.D8, LCD1.DB4
  N6: Part1.D9_PWM, LCD1.DB5
  N7: Part1.D10_PWM/SS, LCD1.DB6
  N8: Part1.D11_PWM/MOSI, LCD1.DB7
  N9: Part1.D12/MISO, LCD1.E
  N10: Part1.D13/SCK, LCD1.RS
  N11: Part1.D2, S1.Pin_3, S1.Pin_4
  N12: Part1.D3_PWM, IC2.pin15
  N13: Part1.D7, IC2.pin10
  N14: LCD1.VSS, LCD1.R/W, VCC1.-, IC2.pin9, MIC1.pin2, R4.Pin_1
  N15: LCD1.VDD, VCC1.+, IC2.pin18, C2.1
  N16: LCD1.V0, R4.Pin_0
  N17: S1.Pin_1, S1.Pin_2
  N18: IC2.pin1, IC2.pin4
  N19: IC2.pin2, R1.Pin_0, R2.Pin_1
  N20: IC2.pin3, R2.Pin_0
  N21: IC2.pin7, XTAL1.pin_0
  N22: IC2.pin8, XTAL1.pin_1
  N23: IC2.pin16, R3.Pin_1
  N24: IC2.pin17, R3.Pin_0, C2.0
  N25: MIC1.pin1, C1.1
  N26: C1.0, R1.Pin_1
