# Fritzing sketch hold (saved by Fritzing 0.9.0b)
breadboards: 1

parts:
  Part1 = Arduino Uno (Rev3)
  IC2 = IC, DIP package, 18 pins [chip_label=MT8870]
  LCD1 = LCD screen
  S1 = Pushbutton [package="[THT]"]
  R1 = Resistor [tolerance=±5% resistance=220 package=THT]
  Q1 = Basic FET P-Channel [package="TO220 [THT]"]  # not connected
  VCC1 = Battery

nets:
  N1: Part1.A0, IC2.pin11
  N2: Part1.A1, IC2.pin12
  N3: Part1.A2, IC2.pin13
  N4: Part1.A3, IC2.pin14
  N5: Part1.D8, LCD1.DB4
  N6: Part1.D9_PWM, LCD1.DB5
  N7: Part1.D10_PWM/SS, LCD1.DB6
  N8: Part1.D11_PWM/MOSI, LCD1.DB7
  N9: Part1.D12/MISO, LCD1.E
  N10: Part1.D13/SCK, LCD1.RS
  N11: Part1.D2, S1.Pin_3, S1.Pin_4
  N12: Part1.D3_PWM, IC2.pin15
  N13: Part1.D7, IC2.pin10
  N14: LCD1.VSS, LCD1.R/W, VCC1.-
  N15: LCD1.VDD, R1.Pin_1, VCC1.+
  N16: S1.Pin_1, S1.Pin_2, R1.Pin_0
